# Fritzing sketch digitalwk11 (saved by Fritzing 0.9.3b)
breadboards: 1

parts:
  元件1 = Arduino Uno (Rev3) - ICSP
  R1 = Resistor [tolerance=±5% resistance=220 package=THT]
  R2 = Resistor [tolerance=±5% resistance=220 package=THT]
  LED1 = LED - 5mm [color="Red (633nm)" package="5 mm [THT]"]
  LED2 = LED - 5mm [color="Red (633nm)" package="5 mm [THT]"]

nets:
  N1: 元件1.D13/SCK, LED2.anode
  N2: 元件1.GND, R1.Pin_0, R2.Pin_0
  N3: R1.Pin_1, LED1.cathode
  N4: R2.Pin_1, LED2.cathode
